# Fritzing sketch FlatSub-Wiring (saved by Fritzing 1.0.1rc)
breadboards: 1

parts:
  Part1 = Arduino Mega 2560 (Rev3)
  FS-IA6B = fs R6A
  D1 = Diode [package=diode-1n4148]
  L298N1 = L298N DC motor driver
  Screw = DC Motor with two-phase hall-encoder [part_number=VT-E-G25A-06-177E]
  6v = RioRand LM2596
  12v = RioRand LM2596
  BAT1 = BC9VPC [package=bc9vpc]
  Part2 = 16-Channel 12-bit PWM Servo Driver - I2C [part_number=815]
  Rudder = Basic Servo
  DivePlane = Basic Servo
  Ballast_Pump = water pump/motor
  RY1 = KF-301 Relay [package=THT]
  Water_Valve = Solenoid
  Diode_(prevent_emf) = DIODE-ZENER [package=diode-zener]

nets:
  N1: Part1.D21/SCL, Part2.SCL
  N2: Part1.D20/SDA, Part2.SDA
  N3: Part1.D19/RX1, FS-IA6B.Pin_3
  N4: Part1.D17_PWM/RX2, FS-IA6B.Pin_12
  N5: Part1.D16_PWM/TX2, D1.C
  N6: Part1.D11_PWM, L298N1.ENB
  5V: Part1.5V, FS-IA6B.Pin_6, Screw.pin5, Part2.VCC, RY1.power
  GND: Part1.GND, FS-IA6B.Pin_9, L298N1.GND, Screw.pin4, 6v.Pin_4, 12v.Pin_4, Part2.GND, Rudder.gnd, DivePlane.gnd, RY1.ground
  VIN: Part1.VIN, L298N1.12V, 12v.Pin_3
  N7: Part1.D2_PWM, Screw.pin3
  N8: Part1.D3_PWM, Screw.pin6
  N9: Part1.D22, L298N1.IN3
  N10: Part1.D23, L298N1.IN4
  N11: Part1.D24, L298N1.IN2
  N12: Part1.D25, L298N1.IN1
  N13: Part1.D27, RY1.signal
  N14: L298N1.OUT1, Ballast_Pump.pin_2
  N15: L298N1.OUT2, Ballast_Pump.pin_1
  N16: L298N1.OUT3, Screw.pin2
  N17: L298N1.OUT4, Screw.pin1
  N18: L298N1.5V, L298N1.ENA
  N19: 6v.Pin_1, 12v.Pin_1, BAT1.V+
  N20: 6v.Pin_2, 12v.Pin_2, BAT1.V-
  N21: 6v.Pin_3, Part2.PWRIN
  N22: Part2.PWM1, DivePlane.pulse
  VCC: Part2.5.0V, Rudder.vcc, DivePlane.vcc
  N23: Part2.PWM0, Rudder.pulse
  N24: RY1.C, Water_Valve.pin1, Diode_(prevent_emf).A
  N25: RY1.NO, Water_Valve.pin2, Diode_(prevent_emf).C

custom parts:
  fs R6A: FS R6A RC receiver.
  L298N DC motor driver: 2x DC motor driver with 78M05 positive voltage regulator (7..35 V) L298N: max 46 V, 2 A Set 5 V Enable jumper to enable 5 V regultor (needed for the L298N) and +5 V output at screw terminal or supply external +5 V at screw terminal Set ENA and/or ENB to +5 V to enable motor permanently or supply ENA and/or ENB with PWM signal IN1 and IN2 set rotation directory for motor A (OUT1/OUT2) IN2 and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
  16-Channel 12-bit PWM Servo Driver - I2C: You want to make a cool robot, maybe a hexapod walker, or maybe just a piece of art with a lot of moving parts. Or maybe you want to drive a lot of LEDs with precise PWM output. Using only two pins, control 16 free-running PWM outputs! You can even chain up 62 breakouts to control up to 992 PWM outputs.
  water pump/motor: WATER PUMP BY ARDUBLOCKTR
  KF-301 Relay: KF-301 SPDT Relay module using SRD-05VDC-SL-C relay.
